// Logisim project 8 bit alu.circ as structural Verilog: 2 circuits, main circuit main
module main (
  input  in_1,
  input  in_2,
  input  in_3,
  input  in_4,
  input  in_5,
  input  in_6,
  input  in_7,
  input  in_8,
  input  in_9,
  input  in_10,
  input  in_11,
  input  in_12,
  input  in_13,
  input  in_14,
  input  in_15,
  input  in_16,
  input  in_17,
  input  in_18,
  output out_19,
  output out_20,
  output out_21,
  output out_22,
  output out_23,
  output out_24,
  output out_25,
  output out_26,
  output out_27,
  output out_28,
  output out_29,
  output out_30,
  output out_31,
  output out_32,
  output out_33,
  output out_34,
  output out_35,
  output out_36
);

  wire adder_1_cout, adder_2_cout, adder_3_cout, adder_4_cout, adder_5_cout, adder_6_cout, adder_7_cout,
       subtractor_1_bout, subtractor_1_out, subtractor_2_bout, subtractor_2_out, subtractor_3_bout,
       subtractor_3_out, subtractor_4_bout, subtractor_4_out, subtractor_5_bout, subtractor_5_out,
       subtractor_6_bout, subtractor_6_out, subtractor_7_bout, subtractor_7_out, subtractor_8_bout,
       subtractor_8_out;

  Subtractor #(.width(1)) subtractor_1 (
    .a(in_3), .b(in_11), .out(subtractor_1_out), .bout(subtractor_1_bout));  // open: bin
  Subtractor #(.width(1)) subtractor_2 (
    .a(in_4), .b(in_12), .out(subtractor_2_out), .bin(subtractor_1_bout), .bout(subtractor_2_bout));
  Subtractor #(.width(1)) subtractor_3 (
    .a(in_5), .b(in_13), .out(subtractor_3_out), .bin(subtractor_2_bout), .bout(subtractor_3_bout));
  Subtractor #(.width(1)) subtractor_4 (
    .a(in_6), .b(in_14), .out(subtractor_4_out), .bin(subtractor_3_bout), .bout(subtractor_4_bout));
  Subtractor #(.width(1)) subtractor_5 (
    .a(in_7), .b(in_15), .out(subtractor_5_out), .bin(subtractor_4_bout), .bout(subtractor_5_bout));
  Subtractor #(.width(1)) subtractor_6 (
    .a(in_8), .b(in_16), .out(subtractor_6_out), .bin(subtractor_5_bout), .bout(subtractor_6_bout));
  Subtractor #(.width(1)) subtractor_7 (
    .a(in_9), .b(in_17), .out(subtractor_7_out), .bin(subtractor_6_bout), .bout(subtractor_7_bout));
  Subtractor #(.width(1)) subtractor_8 (
    .a(in_10), .b(in_18), .out(subtractor_8_out), .bin(subtractor_7_bout), .bout(subtractor_8_bout));
  Adder #(.width(1)) adder_1 (.a(in_3), .b(in_11), .out(out_19), .cout(adder_1_cout));  // open: cin
  Adder #(.width(1)) adder_2 (.a(in_4), .b(in_12), .out(out_20), .cin(adder_1_cout), .cout(adder_2_cout));
  Adder #(.width(1)) adder_3 (.a(in_5), .b(in_13), .out(out_21), .cin(adder_2_cout), .cout(adder_3_cout));
  Adder #(.width(1)) adder_4 (.a(in_6), .b(in_14), .out(out_22), .cin(adder_3_cout), .cout(adder_4_cout));
  Adder #(.width(1)) adder_5 (.a(in_7), .b(in_15), .out(out_23), .cin(adder_4_cout), .cout(adder_5_cout));
  Adder #(.width(1)) adder_6 (.a(in_8), .b(in_16), .out(out_24), .cin(adder_5_cout), .cout(adder_6_cout));
  Adder #(.width(1)) adder_7 (.a(in_9), .b(in_17), .out(out_25), .cin(adder_6_cout), .cout(adder_7_cout));
  Adder #(.width(1)) adder_8 (.a(in_10), .b(in_18), .out(out_26), .cin(adder_7_cout), .cout(out_27));
  Multiplexer #(.disabled(0), .enable("false")) multiplexer_1 (
    .in0(out_19), .in1(subtractor_1_out), .out(out_28), .sel(in_2));
  Multiplexer #(.disabled(0), .enable("false")) multiplexer_2 (
    .in0(out_20), .in1(subtractor_2_out), .out(out_29), .sel(in_2));
  Multiplexer #(.disabled(0), .enable("false")) multiplexer_3 (
    .in0(out_21), .in1(subtractor_3_out), .out(out_30), .sel(in_2));
  Multiplexer #(.disabled(0), .enable("false")) multiplexer_4 (
    .in0(out_22), .in1(subtractor_4_out), .out(out_31), .sel(in_2));
  Multiplexer #(.disabled(0), .enable("false")) multiplexer_5 (
    .in0(out_23), .in1(subtractor_5_out), .out(out_32), .sel(in_2));
  Multiplexer #(.disabled(0), .enable("false")) multiplexer_6 (
    .in0(out_24), .in1(subtractor_6_out), .out(out_33), .sel(in_2));
  Multiplexer #(.disabled(0), .enable("false")) multiplexer_7 (
    .in0(out_25), .in1(subtractor_7_out), .out(out_34), .sel(in_2));
  Multiplexer #(.disabled(0), .enable("false")) multiplexer_8 (
    .in0(out_26), .in1(subtractor_8_out), .out(out_35), .sel(in_2));
  Multiplexer #(.disabled(0), .enable("false")) multiplexer_9 (
    .in0(out_27), .in1(subtractor_8_bout), .out(out_36), .sel(in_2));
endmodule

module _8_bit_adder (
  input  in_1,
  input  in_2,
  input  in_3,
  input  in_4,
  input  in_5,
  input  in_6,
  input  in_7,
  input  in_8,
  input  in_9,
  input  in_10,
  input  in_11,
  input  in_12,
  input  in_13,
  input  in_14,
  input  in_15,
  input  in_16,
  output out_17,
  output out_18,
  output out_19,
  output out_20,
  output out_21,
  output out_22,
  output out_23,
  output out_24,
  output out_25
);

  wire adder_1_cout, adder_2_cout, adder_3_cout, adder_4_cout, adder_5_cout, adder_6_cout, adder_7_cout;

  Adder #(.width(1)) adder_1 (.a(in_1), .b(in_9), .out(out_17), .cout(adder_1_cout));  // open: cin
  Adder #(.width(1)) adder_2 (.a(in_2), .b(in_10), .out(out_18), .cin(adder_1_cout), .cout(adder_2_cout));
  Adder #(.width(1)) adder_3 (.a(in_3), .b(in_11), .out(out_19), .cin(adder_2_cout), .cout(adder_3_cout));
  Adder #(.width(1)) adder_4 (.a(in_4), .b(in_12), .out(out_20), .cin(adder_3_cout), .cout(adder_4_cout));
  Adder #(.width(1)) adder_5 (.a(in_5), .b(in_13), .out(out_21), .cin(adder_4_cout), .cout(adder_5_cout));
  Adder #(.width(1)) adder_6 (.a(in_6), .b(in_14), .out(out_22), .cin(adder_5_cout), .cout(adder_6_cout));
  Adder #(.width(1)) adder_7 (.a(in_7), .b(in_15), .out(out_23), .cin(adder_6_cout), .cout(adder_7_cout));
  Adder #(.width(1)) adder_8 (.a(in_8), .b(in_16), .out(out_24), .cin(adder_7_cout), .cout(out_25));
endmodule
